// Logisim project seq_circuit.circ as structural Verilog: 1 circuit, main circuit main
module main (
  input  x,
  input  y,
  input  c,
  output sum,
  output carry
);

  wire and_1_out, and_2_out, clock_1_out, d_ff_1_q, undriven, xor_1_out;

  Clock clock_1 (.out(clock_1_out));
  D_Flip_Flop d_ff_1 (.clk(clock_1_out), .D(undriven), .Q(d_ff_1_q));  // open: Qn, preset, en, reset
  xor xor_1 (xor_1_out, x, y);
  and and_1 (and_1_out, x, y);
  xor xor_2 (sum, xor_1_out, c);
  and and_2 (and_2_out, xor_1_out, c);
  or or_1 (carry, and_2_out, and_1_out);
endmodule
